# Fritzing sketch APDS-9960_Gesture (saved by Fritzing 0.9.3b)

parts:
  Part1 = Adafruit APDS-9960 [part_number="Adafruit #3595"]
  Part2 = Arduino Nano (Rev3.0) (ICSP)

nets:
  3.3V: Part1.3.3V, Part2.3V3
  GND: Part1.GND, Part2.GND
  N1: Part1.SCL, Part2.A5
  N2: Part1.SDA, Part2.A4
  N3: Part1.INT, Part2.D2

custom parts:
  Adafruit APDS-9960: The APDS9960 from Avago Technologies has an integrated IR LED and driver, along with four directional photodiodes that sense reflected IR energy from the LED. It's proximity detection feature allows it to measure the distance an object is from the front of the sensor (up to a few centimeters) with 8 bit resolution. Since there are four IR sensors, you can measure the changes in light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
