# Fritzing sketch Autodesk Fusion Joystick (saved by Fritzing 0.9.4)

parts:
  Part1 = Black Joystick KY-023
  Part2 = Arduino Pro Micro (Clone)

nets:
  N1: Part1.SW, Part2.D2
  N2: Part1.VRy, Part2.A1
  N3: Part1.VRx, Part2.A0
  +5V: Part1.+5V, Part2.VCC
  GND: Part1.GND, Part2.GND

custom parts:
  Black Joystick KY-023: Description: The joystick is a combination of 2 analoog potentiometer and a digital switch. Arduino GND --> Module pin - Arduino +5V --> Module pin +5V Arduino Analoog 0 --> Module VRx Arduino Analoog 1 --> Module VRy Arduino Digital --> Module SW Dimensions: 1" x 1.25"
