# Fritzing sketch Bluetooth_HC-06 (saved by Fritzing 0.9.3b)
breadboards: 1

parts:
  Part1 = Arduino Nano (Rev3.0)
  Part2 = Bluetooth HC-05 Macho
  LED1 = smd LED [color="Red (633nm)" package="0603 [SMD]"]
  Grove1 = Grove OLED 128x96

nets:
  N1: Part1.D1/TX, Part2.RXD
  N2: Part1.D0/RX, Part2.TXD
  N3: Part1.D2, LED1.anode
  GND: Part1.GND, Part2.GND, LED1.cathode, Grove1.GND
  VCC: Part1.5V, Part2.VCC, Grove1.VCC
  N4: Part1.A5, Grove1.SCL
  N5: Part1.A4, Grove1.SDA
