# Fritzing sketch Bluetooth_relay (saved by Fritzing 0.9.3b)
breadboards: 1

parts:
  Part1 = Arduino Nano (Rev3.0)
  Part2 = Bluetooth HC-05 Macho
  Relay_5V1 = Keyes Relay [package=THT]

nets:
  N1: Part1.D1/TX, Part2.RXD
  N2: Part1.D0/RX, Part2.TXD
  N3: Part1.D2, Relay_5V1.signal
  GND: Part1.GND, Part2.GND, Relay_5V1.ground
  5V: Part1.5V, Part2.VCC

custom parts:
  Keyes Relay: The Keyes 5V relay module is suitable for SCM development, home appliance control. It uses a 5V~12V TIL control signal which can control DC / AC signal.
