# Fritzing sketch Button_State (saved by Fritzing 0.9.3b)
breadboards: 1

parts:
  S1 = Pushbutton [package="[SMD]"]
  LED1 = LED - 3mm [color="Red (633nm)" package="3 mm [THT]"]
  Part1 = Arduino Nano (Rev3.0) (ICSP)
  R1 = Resistor [tolerance=±5% resistance=220 package="2512 [SMD]"]

nets:
  N1: S1.Pin_1, S1.Pin_2, LED1.cathode, Part1.GND
  N2: S1.Pin_3, S1.Pin_4, Part1.D5
  N3: LED1.anode, R1.Pin_0
  N4: Part1.D2, R1.Pin_1
