# Fritzing sketch DIY_Antenli_LED_Button_Receiver (saved by Fritzing 0.9.4)

parts:
  Part1 = Arduino Nano (Rev3.0)
  nRF24L01_+_Antenna1 = nRF24L01+Antenna [chip_label=IC package="DIP (Dual Inline) [THT]"]  # not connected
  nRF24L01_Adapter1 = nRF24L01 Adapter [chip_label=IC package="DIP (Dual Inline) [THT]"]
  LED1 = smd LED [color="Red (633nm)" package="0603 [SMD]"]

nets:
  GND: Part1.GND, nRF24L01_Adapter1.gnd, LED1.cathode
  N1: Part1.D2, LED1.anode
  N2: Part1.D8, nRF24L01_Adapter1.csn
  N3: Part1.D9, nRF24L01_Adapter1.ce
  N4: Part1.D11/MOSI, nRF24L01_Adapter1.mosi
  N5: Part1.D12/MISO, nRF24L01_Adapter1.miso
  5V: Part1.5V, nRF24L01_Adapter1.vcc
  N6: Part1.D13/SCK, nRF24L01_Adapter1.sck

custom parts:
  nRF24L01+Antenna: A DIP stand-in part for whatever IC you want. With 8 pins on a 300mil dual inline package (DIP) footprint.
  nRF24L01 Adapter: A DIP stand-in part for whatever IC you want. With 8 pins on a 300mil dual inline package (DIP) footprint.
