# Fritzing sketch ESP-01 OLED (saved by Fritzing 0.9.4)

parts:
  U1 = ESP8266 WiFi Module [part_number=ESP8266]
  Grove1 = Grove OLED 128x96
  Power_plug1 = Power plug  # not connected

nets:
  N1: U1.GPIO_0, Grove1.SDA
  N2: U1.GPIO_2, Grove1.SCL

custom parts:
  ESP8266 WiFi Module: Generic WiFi Module based on the ESP8266 with onboard PCB antenna and UART communications
