# Fritzing sketch ESP-01 wifi hall effect (saved by Fritzing 0.9.4)

parts:
  U1 = ESP8266-01S [part_number=ESP8266]
  U2 = LIPO-110mAh [package=lipo-110]
  Mod1 = KY-003 Hall Magnetic Sensor Module [package="Breakout board"]
  Power_plug1 = Power plug
  LED2 = LEDs [package=led10mm]

nets:
  N1: U1.RXD, LED2.A
  N2: U1.VCC, U1.CH_PD, U2.+
  N3: U1.GPIO_2, Mod1.S
  N4: U1.GND, U2.-, LED2.C
  N5: Mod1.-, Power_plug1.GND
  VIN: Mod1.Vin, Power_plug1.VCC

custom parts:
  KY-003 Hall Magnetic Sensor Module: KEYES KY-003 Arduino Hall Magnetic Sensor Module is a switch that will turn on/off in the presence of a magnetic field.
