# Fritzing sketch ESP-01_micro_switch_wifi (saved by Fritzing 0.9.4)
breadboards: 1

parts:
  U1 = ESP8266-01S [part_number=ESP8266]
  Switch1 = Switch with Pull-Up and LED
  U2 = LIPO-2000mAh [package=lipo-2000]
  LED1 = LED - 5mm [color="Red (633nm)" package="5 mm [THT]"]
  R1 = Resistor [tolerance=±5% resistance=220 package=THT]

nets:
  VCC: U1.VCC, U1.CH_PD, Switch1.VCC, U2.+
  N1: U1.GPIO_0, LED1.anode
  N2: U1.GPIO_2, Switch1.OUT
  GND: U1.GND, Switch1.GND, U2.-, R1.Pin_0
  N3: LED1.cathode, R1.Pin_1
