# Fritzing sketch ESP32CAM_Telegram_Camera (saved by Fritzing 0.9.4)

parts:
  ESP32_-_Back1 = ESP32 - CAM
  J1 = Basic Servo
  Power_plug1 = Power plug

nets:
  N1: ESP32_-_Back1.GPIO13, J1.pulse
  GND: ESP32_-_Back1.GND, J1.gnd, Power_plug1.GND
  VCC: ESP32_-_Back1.5V, J1.vcc, Power_plug1.VCC

custom parts:
  ESP32 - CAM: The ESP32-CAM has a very competitive small-size camera module that can operate independently as a minimum system with a footprint of only 27*40.5*4.5mm and a deep sleep current of up to 6mA.
