# Fritzing sketch ESP8266_LED_WIFI (saved by Fritzing 0.9.4)

parts:
  U1 = ESP8266 WiFi Module [part_number=ESP8266]
  LED1 = LED - 5mm [color="Red (633nm)" package="5 mm [THT]"]
  Power_plug1 = Power plug

nets:
  N1: U1.RXD, LED1.anode
  VCC: U1.VCC, U1.CH_PD, Power_plug1.VCC
  GND: U1.GND, Power_plug1.GND

notes:
  3V

custom parts:
  ESP8266 WiFi Module: Generic WiFi Module based on the ESP8266 with onboard PCB antenna and UART communications
