# Fritzing sketch GPS_SDCard_OLED_Nano (saved by Fritzing 0.9.3b)

parts:
  Part1 = Arduino Nano (Rev3.0)
  Part5 = MicroSD Card Module

nets:
  N1: Part1.D5, Part5.CS

notes:
  GY-GPSV3-NEO
  GND - TX - RX - VCC
