# Fritzing sketch HC-SR501 motion sensor (saved by Fritzing 0.9.3b)
breadboards: 1

parts:
  Part1 = Arduino Nano (Rev3.0) (ICSP)
  Part3 = HC-SR501 Body Sensor Module
  LED1 = smd LED [color="Blue (525nm)" package="0603 [SMD]"]
  LED2 = smd LED [color="Yellow (595nm)" package="0603 [SMD]"]
  LED3 = smd LED [color="Red (633nm)" package="0603 [SMD]"]

nets:
  N1: Part1.D7, Part3.OUT
  N2: Part1.D11/MOSI, LED3.anode
  N3: Part1.D12/MISO, LED2.anode
  GND: Part1.GND, Part3.GND, LED1.cathode, LED2.cathode, LED3.cathode
  5V: Part1.5V, Part3.VCC
  N4: Part1.D13/SCK, LED1.anode

custom parts:
  HC-SR501 Body Sensor Module: Pyroelectric Infrared PIR Motion Sensor Detector Module
