# Fritzing sketch Hall_Effect_NodeMCU (saved by Fritzing 0.9.3b)

parts:
  U2 = ESP8266 NodeMCU LoLin module
  LED1 = LED - 5mm [color="Red (633nm)" package="5 mm [THT]"]
  U1 = mystery part, 3 pins [chip_label=Hall]
  R1 = Resistor [tolerance=±5% resistance=220 package=THT]

nets:
  N1: U2.D2, R1.Pin_1
  N2: U2.3V3, U1.pin2
  N3: U2.GND, LED1.cathode, U1.pin1
  N4: U2.D5, U1.pin3

custom parts:
  ESP8266 NodeMCU LoLin module: ESP8266 based NodeMCU
