# Fritzing sketch Keypad_buzzer (saved by Fritzing 0.9.3b)

parts:
  Part1 = Arduino Nano (Rev3.0) (ICSP)
  J1 = Piezo Speaker  # not connected
  Matrix_keypad2 = KEYPAD 4x4

nets:
  N1: Part1.D2, Matrix_keypad2.col1
  N2: Part1.D3, Matrix_keypad2.col2
  N3: Part1.D4, Matrix_keypad2.col3
  N4: Part1.D5, Matrix_keypad2.col4
  N5: Part1.D6, Matrix_keypad2.row1
  N6: Part1.D7, Matrix_keypad2.row2
  N7: Part1.D8, Matrix_keypad2.row3
  N8: Part1.D9, Matrix_keypad2.row4

custom parts:
  KEYPAD 4x4: Matrix keypad 16 buttons, 4 rows x 4 columns
