# Fritzing sketch Lazer topu (saved by Fritzing 0.9.3b)
breadboards: 1

parts:
  LD1 = LD
  J2 = Basic Servo
  Grove1 = Grove OLED 128x96
  Part2 = NRF24L01+ Breakout Board
  Part3 = Arduino Nano (Rev3.0) (ICSP)
  Power_plug1 = Power plug
  J1 = Basic Servo
  U1 = POT [package=alps_pot]
  U2 = POT [package=alps_pot]

nets:
  GND: LD1.cathode, J2.gnd, Grove1.GND, Part2.GND, Part3.GND, Power_plug1.GND, J1.gnd
  VCC: J2.vcc, Grove1.VCC, Part2.VCC, Power_plug1.VCC, J1.vcc, U1.E
  N1: Grove1.SDA, Part3.A4
  N2: Grove1.SCL, Part3.A5
  N3: Part2.CE, Part3.D7
  N4: Part2.CS, Part3.D8
  N5: Part2.SCK, Part3.D13/SCK
  N6: Part2.MOSI, Part3.D11/MOSI
  N7: Part2.MISO, Part3.D12/MISO
  N8: Part3.A1, U2.S
  N9: Part3.A0, U1.S
  N10: U1.A, U2.A

notes:
  CE
  SCK
  MISO
  MOSI
  CS

custom parts:
  LD: A Generic Red Dot Laser Diode Module (~5mW)
