# Fritzing sketch Lazer_kapani_receiver (saved by Fritzing 0.9.3b)
breadboards: 1

parts:
  Grove2 = Grove OLED 128x96
  Part4 = NRF24L01+ Breakout Board
  Part5 = Arduino Nano (Rev3.0) (ICSP)
  LED1 = LED - 5mm [color="Red (633nm)" package="5 mm [THT]"]
  R1 = Resistor [tolerance=±5% resistance=220 package=THT]
  Part9 = KY-008 Laser Transmitter Module [package="Breakout board"]

nets:
  GND: Grove2.GND, Part4.GND, Part5.GND, LED1.cathode, Part9.-
  VCC: Grove2.VCC, Part4.VCC, Part5.5V
  N1: Grove2.SDA, Part5.A4
  N2: Grove2.SCL, Part5.A5
  N3: Part4.CE, Part5.D7
  N4: Part4.CS, Part5.D8
  N5: Part4.SCK, Part5.D13/SCK
  N6: Part4.MOSI, Part5.D11/MOSI
  N7: Part4.MISO, Part5.D12/MISO
  N8: Part5.D2, R1.Pin_1
  N9: Part5.D9, Part9.S

notes:
  CS
  MOSI
  MISO
  SCK
  CE

custom parts:
  KY-008 Laser Transmitter Module: Laser Transmitter module KY-008 for Arduino, emits a dot shaped red laser beam.
