# Fritzing sketch Lazer_kapani_transmitter (saved by Fritzing 0.9.3b)
breadboards: 1

parts:
  Part6 = NRF24L01+ Breakout Board
  Part7 = Arduino Nano (Rev3.0) (ICSP)

nets:
  GND: Part6.GND, Part7.GND
  VCC: Part6.VCC, Part7.5V
  N1: Part6.CE, Part7.D7
  N2: Part6.CS, Part7.D8
  N3: Part6.SCK, Part7.D13/SCK
  N4: Part6.MOSI, Part7.D11/MOSI
  N5: Part6.MISO, Part7.D12/MISO

notes:
  CS
  MOSI
  MISO
  SCK
  CE
  Laser Receiver
