# Fritzing sketch MPU6050_Gyro_sensor (saved by Fritzing 0.9.3b)

parts:
  Part1 = Arduino Nano (Rev3.0) (ICSP)
  GY1 = MPU-6050 Board GY-521 [form="♀ (female)" package=THT]

nets:
  N1: Part1.GND, GY1.pin2
  N2: Part1.5V, GY1.pin1
  N3: Part1.A5, GY1.pin3
  N4: Part1.A4, GY1.pin4

custom parts:
  MPU-6050 Board GY-521: Acelerometro y Giroscopio MPU-6050 Board GY-521
