# Fritzing sketch NodeMCU Relay (saved by Fritzing 0.9.3b)

parts:
  U1 = NodeMCU V1.0
  U2 = 2-Channel 5v Relay Shield [package=relay-2ch5v10a]

nets:
  N1: U1.D1, U2.IN1
  N2: U1.D2, U2.IN2
  3V3: U1.3V3, U2.VCC
  GND: U1.GND, U2.GND

custom parts:
  NodeMCU V1.0: ESP8266 based NodeMCU
  2-Channel 5v Relay Shield: 2 Channel 5v Relay Shield w. 2x SPD-06VDC-SD-C
