# Fritzing sketch NodeMCU_Host_Client (saved by Fritzing 0.9.3b)

parts:
  U4 = ESP8266 NodeMCU LoLin module
  LED2 = LED - 5mm [color="Red (633nm)" package="5 mm [THT]"]
  S1 = Pushbutton [package="[THT]"]

nets:
  N1: U4.D2, LED2.anode
  N2: U4.D4, S1.Pin_3, S1.Pin_4
  N3: U4.GND, LED2.cathode, S1.Pin_1, S1.Pin_2

custom parts:
  ESP8266 NodeMCU LoLin module: ESP8266 based NodeMCU
