# Fritzing sketch OLED_DS3231 clock sensor (saved by Fritzing 0.9.3b)

parts:
  Part1 = Arduino Nano (Rev3.0) (ICSP)
  ZS-042_RTC1 = ZS-042 RTC Module
  Grove1 = Grove OLED 128x96  # not connected

nets:
  GND: Part1.GND, ZS-042_RTC1.GND
  5V: Part1.5V, ZS-042_RTC1.VCC
  N1: Part1.A5, ZS-042_RTC1.SCL
  N2: Part1.A4, ZS-042_RTC1.SDA
