# Fritzing sketch OLED_Sicaklik_Nem (saved by Fritzing 0.9.3b)
breadboards: 1

parts:
  Part1 = Arduino Uno (Rev3)
  S1 = Pushbutton [package="[THT]"]
  RHT1 = Humidity and Temperature Sensor RHT03
  Grove1 = Grove OLED 128x96

nets:
  N1: Part1.A4/SDA, Grove1.SDA
  N2: Part1.A5/SCL, Grove1.SCL
  N3: Part1.D12/MISO, S1.Pin_1, S1.Pin_2
  GND: Part1.GND, S1.Pin_3, S1.Pin_4, RHT1.GND_1, Grove1.GND
  N4: Part1.D2, RHT1.Vcc
  5V: Part1.5V, RHT1.Data-signal, Grove1.VCC

custom parts:
  Humidity and Temperature Sensor RHT03: Digital relative humidity & temperature sensor RHT03
