# Fritzing sketch Refleks oyunu (saved by Fritzing 0.9.3b)
breadboards: 3

parts:
  Part1 = Arduino Uno (Rev3)
  S1 = Pushbutton [package="[SMD]"]
  S2 = Pushbutton [package="[SMD]"]
  S3 = Pushbutton [package="[SMD]"]
  Grove1 = Grove OLED 128x96
  LED1 = LED - 5mm [color="Red (633nm)" package="5 mm [THT]"]
  R1 = Resistor [tolerance=±5% resistance=220 package="2512 [SMD]"]

nets:
  N1: Part1.A4/SDA, Grove1.SDA
  N2: Part1.A5/SCL, Grove1.SCL
  N3: Part1.D8, S2.Pin_3, S2.Pin_4
  N4: Part1.D9_PWM, S1.Pin_3, S1.Pin_4
  N5: Part1.D12/MISO, LED1.anode
  N6: Part1.D13/SCK, S3.Pin_3, S3.Pin_4
  5V: Part1.5V, Grove1.VCC
  GND: Part1.GND, S1.Pin_1, S1.Pin_2, S2.Pin_1, S2.Pin_2, S3.Pin_1, S3.Pin_2, Grove1.GND, R1.Pin_0
  N7: LED1.cathode, R1.Pin_1
