# Fritzing sketch Saatli_OLEDli_kutu (saved by Fritzing 0.9.3b)

parts:
  Grove1 = Grove OLED 128x96
  Grove2 = Grove OLED 128x96
  Part2 = Adafruit TCA9548A
  ZS-042_RTC1 = ZS-042 RTC Module
  RHT1 = Humidity and Temperature Sensor RHT03
  Part3 = Arduino Mega 2560 (Rev3)

nets:
  N1: Grove1.SDA, Part2.1SDA
  N2: Grove1.SCL, Part2.1SCL
  N3: Grove2.SDA, Part2.0SDA
  N4: Grove2.SCL, Part2.0SCL
  N5: Part2.2SDA, ZS-042_RTC1.SDA
  N6: Part2.2SCL, ZS-042_RTC1.SCL
  N7: Part2.INPUTSDA, Part3.D20/SDA
  N8: Part2.INPUTSCL, Part3.D21/SCL
  N9: RHT1.Data-signal, Part3.D13_PWM

notes:
  Clock
  OLED1
  OLED2
  Multiplexer
  DHT

custom parts:
  Adafruit TCA9548A: You just found the perfect I2C sensor, and you want to wire up two or three or more of them to your Arduino when you realize "Uh oh, this chip has a fixed I2C address, and from what I know about I2C, you cannot have two devices with the same address on the same SDA/SCL pins!" Are you out of luck? You would be, if you didn't have this ultra-cool TCA9548A 1-to-8 I2C multiplexer! Finally, a way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
