# Fritzing sketch Saatli_OLEDli_kutu_v2 (saved by Fritzing 0.9.3b)
breadboards: 1

parts:
  Grove1 = Grove OLED 128x96
  Grove2 = Grove OLED 128x96
  ZS-042_RTC1 = ZS-042 RTC Module
  RHT1 = Humidity and Temperature Sensor RHT03
  Part3 = Arduino Mega 2560 (Rev3)

nets:
  N1: Grove1.SDA, Grove2.SDA, ZS-042_RTC1.SDA, Part3.D20/SDA
  N2: Grove1.SCL, Grove2.SCL, ZS-042_RTC1.SCL, Part3.D21/SCL
  N3: RHT1.Data-signal, Part3.D13_PWM

notes:
  Clock
  OLED1
  OLED2
  DHT
