# Fritzing sketch Saatli_OLEDli_kutu_v2_test (saved by Fritzing 0.9.3b)
breadboards: 1

parts:
  Grove1 = Grove OLED 128x96
  Grove2 = Grove OLED 128x96
  ZS-042_RTC1 = ZS-042 RTC Module
  RHT1 = Humidity and Temperature Sensor RHT03
  Part3 = Arduino Mega 2560 (Rev3)
  Part4 = MicroSD Card Module
  S1 = Momentary Switch [package=ksa_sealed_tac_switch]
  S2 = Momentary Switch [package=ksa_sealed_tac_switch]
  LED1 = smd LED [color="Red (633nm)" package="1206 [SMD]"]

nets:
  N1: Grove1.SDA, Grove2.SDA, ZS-042_RTC1.SDA, Part3.D20/SDA
  N2: Grove1.SCL, Grove2.SCL, ZS-042_RTC1.SCL, Part3.D21/SCL
  N3: RHT1.Data-signal, Part3.D13_PWM
  N4: Part3.GND, LED1.cathode
  N5: Part3.D12_PWM, S1.2
  N6: Part3.D11_PWM, S2.2
  N7: Part3.D10_PWM, LED1.anode
  N8: Part3.D50, Part4.MISO
  N9: Part3.D51, Part4.MOSI
  N10: Part3.D52, Part4.SCK
  N11: Part3.D53, Part4.CS

notes:
  Clock
  OLED1
  OLED2
  DHT
  Micro SD
