# Fritzing sketch TCA9548A_multiplexer_OLED (saved by Fritzing 0.9.3b)

parts:
  Part1 = Arduino Nano (Rev3.0)
  Grove1 = Grove OLED 128x96
  Grove2 = Grove OLED 128x96
  Part2 = Adafruit TCA9548A

nets:
  GND: Part1.GND, Part2.GND
  5V: Part1.5V, Part2.VCC
  N1: Part1.A5, Part2.INPUTSCL
  N2: Part1.A4, Part2.INPUTSDA
  N3: Grove1.SDA, Part2.0SDA
  N4: Grove1.SCL, Part2.0SCL
  N5: Grove2.SDA, Part2.1SDA
  N6: Grove2.SCL, Part2.1SCL

custom parts:
  Adafruit TCA9548A: You just found the perfect I2C sensor, and you want to wire up two or three or more of them to your Arduino when you realize "Uh oh, this chip has a fixed I2C address, and from what I know about I2C, you cannot have two devices with the same address on the same SDA/SCL pins!" Are you out of luck? You would be, if you didn't have this ultra-cool TCA9548A 1-to-8 I2C multiplexer! Finally, a way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
