# Fritzing sketch Thingspeak_Read_OLED (saved by Fritzing 0.9.3b)

parts:
  U1 = ESP8266 NodeMCU LoLin module
  Grove1 = Grove OLED 128x96

nets:
  N1: U1.D1, Grove1.SCL
  N2: U1.D2, Grove1.SDA
  3V3: U1.3V3, Grove1.VCC
  GND: U1.GND, Grove1.GND

custom parts:
  ESP8266 NodeMCU LoLin module: ESP8266 based NodeMCU
