# Fritzing sketch WIFI_AT_Command (saved by Fritzing 0.9.3b)

parts:
  Part1 = Arduino Nano (Rev3.0)
  U2 = ESP8266 WiFi Module [part_number=ESP8266]
  Power_plug1 = Power plug

nets:
  GND: Part1.GND, U2.GND, Power_plug1.GND
  N1: Part1.D8, U2.TXD
  N2: Part1.D9, U2.RXD

custom parts:
  ESP8266 WiFi Module: Generic WiFi Module based on the ESP8266 with onboard PCB antenna and UART communications
