# Fritzing sketch WIFI_LED (saved by Fritzing 0.9.3b)
breadboards: 1

parts:
  U2 = ESP8266 WiFi Module [part_number=ESP8266]
  Part1 = Arduino Nano (Rev3.0)
  LED1 = LED - 3mm [color="Red (633nm)" package="3 mm [THT]"]

nets:
  N1: U2.RXD, Part1.D1/TX
  VCC: U2.VCC, Part1.5V
  GND: U2.GND, Part1.GND, LED1.cathode
  N2: U2.TXD, Part1.D0/RX
  N3: Part1.D5, LED1.anode

notes:
  TX
  RX
  VCC
  Gro

custom parts:
  ESP8266 WiFi Module: Generic WiFi Module based on the ESP8266 with onboard PCB antenna and UART communications
