# Fritzing sketch WIFI_Sicaklik (saved by Fritzing 0.9.3b)
breadboards: 1

parts:
  Part1 = Arduino Nano (Rev3.0)
  RHT2 = Humidity and Temperature Sensor RHT03
  U1 = ESP8266 WiFi Module [part_number=ESP8266]

nets:
  N1: Part1.D1/TX, U1.RXD
  N2: Part1.D0/RX, U1.TXD
  GND: Part1.GND, RHT2.GND_1, U1.GND
  5V: Part1.5V, RHT2.Data-signal, U1.VCC
  N3: Part1.D13/SCK, RHT2.Vcc

notes:
  TX
  RX
  VCC
  Gro

custom parts:
  Humidity and Temperature Sensor RHT03: Digital relative humidity & temperature sensor RHT03
  ESP8266 WiFi Module: Generic WiFi Module based on the ESP8266 with onboard PCB antenna and UART communications
