# Fritzing sketch WIFI_ThingSpeak (saved by Fritzing 0.9.3b)

parts:
  U1 = ESP8266 WiFi Module [part_number=ESP8266]
  Part1 = Arduino Nano (Rev3.0)
  S1 = Pushbutton [package="[SMD]"]
  LED1 = smd LED [color="Red (633nm)" package="1206 [SMD]"]  # not connected

nets:
  N1: U1.RXD, Part1.D1/TX
  VCC: U1.VCC, Part1.5V
  GND: U1.GND, Part1.GND
  N2: U1.TXD, Part1.D0/RX
  N3: Part1.D3, S1.Pin_4

custom parts:
  ESP8266 WiFi Module: Generic WiFi Module based on the ESP8266 with onboard PCB antenna and UART communications
