# Fritzing sketch WIFI_ThingSpeak_Get (saved by Fritzing 0.9.3b)

parts:
  Part1 = Arduino Mega 2560 (Rev3)
  U3 = ESP8266 WiFi Module [part_number=ESP8266]

nets:
  3V3: Part1.3V3, U3.VCC
  GND: Part1.GND, U3.GND
  N1: Part1.D0_RX0, U3.TXD
  N2: Part1.D1_TX0, U3.RXD

custom parts:
  ESP8266 WiFi Module: Generic WiFi Module based on the ESP8266 with onboard PCB antenna and UART communications
