# Fritzing sketch Wireless_2Way (saved by Fritzing 0.9.3b)

parts:
  Part1 = Arduino Nano (Rev3.0)
  Part5 = NRF24L01+ Breakout Board
  S1 = Pushbutton [package="[SMD]"]
  LED1 = smd LED [color="Red (633nm)" package="0805 [SMD]"]

nets:
  GND: Part1.GND, Part5.GND, S1.Pin_3, S1.Pin_4, LED1.cathode
  N1: Part1.D3, S1.Pin_1, S1.Pin_2
  N2: Part1.D4, LED1.anode
  N3: Part1.D7, Part5.CE
  N4: Part1.D8, Part5.CS
  N5: Part1.D11/MOSI, Part5.MOSI
  N6: Part1.D12/MISO, Part5.MISO
  5V: Part1.5V, Part5.VCC
  N7: Part1.D13/SCK, Part5.SCK
