# Fritzing sketch YF_S201_Water_flow_sensor (saved by Fritzing 0.9.3b)

parts:
  YF-S201_Flow_Meter1 = YF-S201 Water Flow Meter
  Part1 = Arduino Nano (Rev3.0)

nets:
  N1: YF-S201_Flow_Meter1.SIG, Part1.D2
  GND: YF-S201_Flow_Meter1.GND, Part1.GND
  VCC: YF-S201_Flow_Meter1.VCC, Part1.5V

custom parts:
  YF-S201 Water Flow Meter: The YF-S201 Flow Meter. The input voltage is 5V to 24V (DC).
