# Fritzing sketch deepsleep-firebase-oled (saved by Fritzing 0.9.4)

parts:
  U1 = XIAO ESP32C3
  OLED1 = OLED 128x64 I2C Monochrome Display GND-VDD
  Switch1 = Switch with Pull-Up and LED

nets:
  N1: U1.D3, Switch1.OUT
  N2: U1.D4, OLED1.SDA
  N3: U1.D5, OLED1.SCK
  3V3: U1.3V3, OLED1.VDD, Switch1.VCC
  GND: U1.GND, OLED1.GND, Switch1.GND

custom parts:
  XIAO ESP32C3: Seeed Studio XIAO ESP32C3 adopts new RISC-V architecture, supporting both Wi-Fi and BLE wireless connectivities. For Internet of Things applications, you will find it is flexible and suitable for all kinds of IoT scenarios.
  OLED 128x64 I2C Monochrome Display GND-VDD: OLED 128x64 I2C Monochrome Display. Note: there are two variants of this part, this one is the GND VDD SCK SDA variant. The other is VDD GND SCK SDA. Make sure you select the part that matches your module as using the incorrect part will probably destroy your module! In addition the mounting holes are marked on silkscreen but not by default drilled. If you want drilled mounting holes, copy a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
