# Fritzing sketch temperature-echo (saved by Fritzing 0.9.4)

parts:
  U1 = XIAO ESP32C3
  Mod1 = KY-015 Temperature & Humidity Sensor Module [package="Breakout board"]
  LED1 = LED - 3mm [color="Red (633nm)" package="3 mm [THT]"]
  R1 = Resistor [tolerance=±5% resistance=220 package="0603 [SMD]"]
  hc-sr1 = hc-sr04

nets:
  N1: U1.D1, hc-sr1.Echo
  N2: U1.D3, R1.Pin_0
  N3: U1.D6, Mod1.S
  N4: U1.D10, hc-sr1.Trig
  3V3: U1.3V3, Mod1.Vin
  GND: U1.GND, Mod1.-, LED1.cathode, hc-sr1.GND
  5V: U1.5V, hc-sr1.VCC
  N5: LED1.anode, R1.Pin_1

custom parts:
  XIAO ESP32C3: Seeed Studio XIAO ESP32C3 adopts new RISC-V architecture, supporting both Wi-Fi and BLE wireless connectivities. For Internet of Things applications, you will find it is flexible and suitable for all kinds of IoT scenarios.
  KY-015 Temperature & Humidity Sensor Module: KY-015 temperature and humidity sensor module, provides a low-latency serial interface to measure humidity and temperature.
